# Fritzing sketch esquema (saved by Fritzing 0.9.2b)
breadboards: 1

parts:
  Componente1 = Arduino Mega 2560 (Rev3)
  Componente2 = LCD Keypad Shield
  Componente3 = Passive Buzzer

nets:
  N1: Componente1.D39, Componente1.D43, Componente1.D47, Componente1.D51, Componente2.+5V
  N2: Componente1.D53, Componente3.S
  GND: Componente1.GND, Componente3.GND

custom parts:
  LCD Keypad Shield: It consists of a 1602 white character blue backlight LCD. The keypad consists of 5 keys — select, up, right, down and left. To save the digital IO pins, the keypad interface uses only one ADC channel. The key value is read through a 5 stage voltage divider.
